# Fritzing sketch FUNGI-TUBE_shield (saved by Fritzing 1.0.4)
circuit board: 12.2542cm x 8.52935cm
breadboards: 5

parts:
  10uF = Ceramic Capacitor [capacitance=10µF voltage=35V package="100 mil [THT, multilayer]"]
  0_1uF = Ceramic Capacitor [capacitance=0.1µF voltage=35V package="100 mil [THT, multilayer]"]
  5v_PS = Power Jack [package=power_jack_pth_lock]
  10uF_2 = Ceramic Capacitor [capacitance=10µF voltage=35V package="100 mil [THT, multilayer]"]
  0_1uF_2 = Ceramic Capacitor [capacitance=0.1µF voltage=35V package="100 mil [THT, multilayer]"]
  LED = LED - 5mm [color="Red (660nm)" current=0.030A package="5 mm [THT]"]
  220ohm = Resistor [tolerance=±5% power=0.25W resistance=220 package=THT]
  ESP32 = ESP32 38Pin narrow
  LLC = I2C level shifter bidirectional
  MicroSD = Adafruit MicroSD card breakout board [part_number="Adafruit #254"]
  RTC = ZS-042 RTC Module
  Multiplexer = Adafruit TCA9548A
  4_7Kohm = Resistor [tolerance=±5% resistance=4.7k package="0603 [SMD]"]
  4_7Kohm_2 = Resistor [tolerance=±5% resistance=4.7k package="0603 [SMD]"]
  ADC = Adafruit ADS1115 16Bit I2C ADC [part_number="Adafruit #1085"]
  Cap = female pin header, 3 pins [form="♀ (female)"]
  RGB = I2C Header [form="♀ (female)" package=THT]
  IR = I2C Header [form="♀ (female)" package=THT]
  CO2 = I2C Header [form="♀ (female)" package=THT]
  VOC = I2C Header [form="♀ (female)" package=THT]
  RH = I2C Header [form="♀ (female)" package=THT]
  GND = female pin header, 8 pins [form="♀ (female)"]

nets:
  VCC: 10uF.0, 0_1uF.0, ESP32.Pin_1, LLC.LV, RTC.VCC, RGB.VCC, IR.VCC
  GND: 10uF.1, 0_1uF.1, 5v_PS.GND, 5v_PS.GNDBREAK, 10uF_2.1, 0_1uF_2.1, LED.cathode, ESP32.Pin_14, ESP32.Pin_32, ESP32.Pin_38, LLC.GND, MicroSD.GND, RTC.GND, Multiplexer.GND, ADC.ADDR, ADC.GND, Cap.pin1, RGB.GND, IR.GND, CO2.GND, VOC.GND, RH.GND, GND.pin1, GND.pin2, GND.pin3, GND.pin4, GND.pin5, GND.pin6, GND.pin7, GND.pin8
  VCC_2: 5v_PS.PWR, 10uF_2.0, 0_1uF_2.0, LLC.HV, MicroSD.VCC, Multiplexer.VCC, 4_7Kohm.Pin_0, 4_7Kohm_2.Pin_0, ADC.VDD, Cap.pin2, CO2.VCC, VOC.VCC, RH.VCC
  N1: LED.anode, 220ohm.Pin_0
  N2: 220ohm.Pin_1, ESP32.Pin_24
  N3: ESP32.Pin_29, MicroSD.CS
  N4: ESP32.Pin_30, MicroSD.CLK
  N5: ESP32.Pin_31, MicroSD.DO
  N6: ESP32.Pin_33, LLC.LV1, RTC.SDA, RGB.SDA, IR.SDA
  N7: ESP32.Pin_36, LLC.LV2, RTC.SCL, RGB.SCL, IR.SCL
  N8: ESP32.Pin_37, MicroSD.DI
  N9: LLC.HV1, Multiplexer.INPUTSDA, 4_7Kohm.Pin_1
  N10: LLC.HV2, Multiplexer.INPUTSCL, 4_7Kohm_2.Pin_1
  N11: Multiplexer.2SDA, VOC.SDA
  N12: Multiplexer.2SCL, VOC.SCL
  N13: Multiplexer.3SDA, RH.SDA
  N14: Multiplexer.3SCL, RH.SCL
  N15: Multiplexer.0SDA, ADC.SDA
  N16: Multiplexer.0SCL, ADC.SCL
  N17: Multiplexer.1SDA, CO2.SDA
  N18: Multiplexer.1SCL, CO2.SCL
  N19: ADC.AIN0, Cap.pin3

notes:
  A
  VCC
  GND
  vcc
  gnd
  scl
  sda
  +
  -
  3v3
  sd1
  sc1
  HV
  LV
  cs
  D1
  D0
  clk
  FUNGI-TUBE Shield v1.2
  P23
  P22
  P21
  P19
  P18
  P5
  P2
  sc0
  sd0
  sd2
  sc2
  sd3
  sc3
  1
  2
  3
  4
  adr
  A0
  Jake Winiski 2025

custom parts:
  ESP32 38Pin narrow: ESP32 38Pin narrow.
  Adafruit MicroSD card breakout board: Not just a simple breakout board, this microSD adapter goes the extra mile - designed for ease of use. Onboard 5v->3v regulator provides 150mA for power-hungry cards 3v level shifting means you can use this with ease on either 3v or 5v systems Uses a proper level shifting chip, not resistors: less problems, and faster read/write access Use 3 or 4 digital pins to read and write 2Gb+ of storage!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
  Adafruit TCA9548A: You just found the perfect I2C sensor, and you want to wire up two or three or more of them to your Arduino when you realize "Uh oh, this chip has a fixed I2C address, and from what I know about I2C, you cannot have two devices with the same address on the same SDA/SCL pins!" Are you out of luck? You would be, if you didn't have this ultra-cool TCA9548A 1-to-8 I2C multiplexer! Finally, a way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
  Adafruit ADS1115 16Bit I2C ADC: For microcontrollers without an analog-to-digital converter or when you want a higher-precision ADC, the ADS1115 provides 16-bit precision at 860 samples/second over I2C. The chip can be configured as 4 single-ended input channels, or two differential channels. As a nice bonus, it even includes a programmable gain amplifier, up to x16, to help boost up smaller single/differential signals to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
